# Fritzing sketch 4-rgb-led (saved by Fritzing 0.7.12b)
breadboards: 1

parts:
  Arduino1 = Arduino
  LED2 = RGB LED (com. anode, rbg) [package="5 mm [THT]"]
  R1 = Resistor [tolerance=±5% resistance=220 package=THT]
  R2 = Resistor [tolerance=±5% resistance=220 package=THT]
  R3 = Resistor [tolerance=±5% resistance=220 package=THT]
  S1 = Pushbutton [package="[THT]"]

nets:
  N1: Arduino1.GND, LED2.common_anode, S1.Pin_1, S1.Pin_2
  N2: Arduino1.D6, R2.Pin_0
  N3: Arduino1.D5, R3.Pin_0
  N4: Arduino1.D3, R1.Pin_0
  N5: Arduino1.D2, S1.Pin_3, S1.Pin_4
  N6: LED2.red_cathode, R2.Pin_1
  N7: LED2.blue_cathode, R3.Pin_1
  N8: LED2.green_cathode, R1.Pin_1
