# Fritzing sketch force-sensor (saved by Fritzing 0.7.12b)
breadboards: 1

parts:
  Arduino1 = Arduino
  R2 = Resistor [tolerance=±5% resistance=10k package=THT]
  J1 = Basic Force Sensing Resistor (FSR) [package=THT]

nets:
  N1: Arduino1.+5V, J1.pin_1
  N2: Arduino1.GND, R2.Pin_0
  N3: Arduino1.A4, R2.Pin_1, J1.pin_0
