# Fritzing sketch light-sensor (saved by Fritzing 0.7.12b)
breadboards: 1

parts:
  Arduino1 = Arduino
  R2 = Resistor [tolerance=±5% resistance=10k package=THT]
  R3 = Photocell (LDR) [package=THT]

nets:
  N1: Arduino1.+5V, R3.pin_0
  N2: Arduino1.GND, R2.Pin_0
  N3: Arduino1.A4, R2.Pin_1, R3.pin_1
