# Fritzing sketch servo-and-variable-resistor (saved by Fritzing 0.7.12b)
breadboards: 1

parts:
  Arduino1 = Arduino
  J1 = Basic Servo
  R1 = Rotary Potentiometer (Small)

nets:
  N1: Arduino1.D6, J1.pulse
  +5V: Arduino1.+5V, J1.vcc, R1.leg1
  GND: Arduino1.GND, J1.gnd, R1.leg2
  N2: Arduino1.A0, R1.wiper
