# Fritzing sketch dcmotor (saved by Fritzing 0.7.12b)
breadboards: 1

parts:
  Arduino1 = Arduino
  R1 = Rotary Potentiometer (Small)
  M2 = DC Motor
  Q1 = NPN-Transistor [package="SOT-23 [SMD]"]
  D1 = Schottky Diode [part_number=1N5817 package="Melf DO-213 AB [SMD]"]
  R2 = 470 Ω Resistor [package=THT]

nets:
  N1: Arduino1.D3, R2.Pin_1
  N2: Arduino1.+5V, R1.leg1, M2.pin_1, D1.cathode
  N3: Arduino1.GND, R1.leg2, Q1.2
  N4: Arduino1.A0, R1.wiper
  N5: M2.pin_2, Q1.1, D1.anode
  N6: Q1.0, R2.Pin_0
